// Logisim project 4bit adder.circ as structural Verilog: 1 circuit, main circuit main
module main (
  input  Cin,
  input  A3,
  input  in_3,
  input  in_4,
  input  A0,
  input  B3,
  input  in_7,
  input  in_8,
  input  B0,
  input  in_10,
  input  in_11,
  input  in_12,
  input  in_13,
  input  in_14,
  input  in_15,
  input  in_16,
  input  in_17
);

  wire and_1_out, and_2_out, and_3_out, and_4_out, and_5_out, and_6_out, and_7_out, and_8_out, and_9_out,
       and_10_out, and_11_out, and_12_out, and_13_out, and_14_out, and_15_out, and_16_out, and_17_out,
       and_18_out, and_19_out, and_20_out, and_21_out, and_22_out, and_23_out, and_24_out, and_25_out,
       and_26_out, and_27_out, and_28_out, and_29_out, and_30_out, and_31_out, and_32_out, and_33_out,
       and_34_out, and_35_out, and_36_out, and_37_out, and_38_out, and_39_out, and_40_out, and_41_out,
       and_42_out, and_43_out, and_44_out, and_45_out, and_46_out, and_47_out, and_48_out, and_49_out,
       and_50_out, and_51_out, and_52_out, and_53_out, and_54_out, and_55_out, and_56_out, and_57_out,
       and_58_out, and_59_out, and_60_out, and_61_out, and_62_out, and_63_out, and_64_out, and_65_out,
       and_66_out, and_67_out, and_68_out, and_69_out, and_70_out, and_71_out, and_72_out, not_1_out,
       not_2_out, not_3_out, not_4_out, not_5_out, not_6_out, not_7_out, not_8_out, or_1_out, or_2_out,
       or_3_out, or_4_out, or_5_out, or_6_out, or_7_out, or_8_out, or_9_out, or_10_out, or_11_out, or_12_out,
       or_13_out, or_14_out, or_15_out, or_16_out, or_17_out, or_18_out, or_19_out, or_20_out, or_21_out,
       or_22_out, or_23_out, or_24_out, xor_1_out, xor_2_out, xor_3_out, xor_4_out, xor_5_out, xor_6_out,
       xor_7_out, xor_8_out;

  not not_1 (not_1_out, A3);
  not not_2 (not_2_out, in_3);
  not not_3 (not_3_out, in_4);
  not not_4 (not_4_out, A0);
  not not_5 (not_5_out, B3);
  not not_6 (not_6_out, in_7);
  not not_7 (not_7_out, in_8);
  not not_8 (not_8_out, B0);
  or or_1 (or_1_out, in_7, in_8);
  or or_2 (or_2_out, in_7, not_7_out, B0);
  and and_1 (and_1_out, or_1_out, B3);
  and and_2 (and_2_out, not_6_out, not_7_out);
  and and_3 (and_3_out, not_5_out, in_8);
  and and_4 (and_4_out, in_7, in_8);
  and and_5 (and_5_out, B3, not_8_out);
  and and_6 (and_6_out, not_5_out, in_7, B0);
  and and_7 (and_7_out, B3, not_6_out, not_7_out);
  and and_8 (and_8_out, not_6_out, not_7_out, not_8_out);
  and and_9 (and_9_out, not_5_out, or_2_out);
  and and_10 (and_10_out, not_7_out, B0);
  and and_11 (and_11_out, B3, not_6_out);
  and and_12 (and_12_out, in_7, not_7_out, B0);
  and and_13 (and_13_out, in_7, in_8, not_8_out);
  and and_14 (and_14_out, not_5_out, not_6_out, not_8_out);
  and and_15 (and_15_out, not_6_out, in_8, B0);
  and and_16 (and_16_out, B3, not_7_out, not_8_out);
  or or_3 (or_3_out, and_2_out, in_8);
  and and_17 (and_17_out, not_5_out, not_6_out);
  and and_18 (and_18_out, not_5_out, not_7_out, not_8_out);
  and and_19 (and_19_out, not_5_out, in_8, B0);
  and and_20 (and_20_out, B3, not_7_out, B0);
  and and_21 (and_21_out, B3, not_6_out, not_8_out);
  and and_22 (and_22_out, not_7_out, not_8_out);
  and and_23 (and_23_out, B3, in_8);
  and and_24 (and_24_out, B3, not_6_out);
  and and_25 (and_25_out, not_5_out, in_7, not_7_out);
  and and_26 (and_26_out, in_7, in_8, not_8_out);
  and and_27 (and_27_out, in_8, not_8_out);
  and and_28 (and_28_out, B0, B3);
  and and_29 (and_29_out, B3, not_6_out);
  and and_30 (and_30_out, not_5_out, in_7, not_7_out);
  and and_31 (and_31_out, not_5_out, not_6_out, in_8);
  or or_4 (or_4_out, and_9_out, and_10_out, and_11_out);
  and and_32 (and_32_out, or_3_out, not_8_out);
  or or_5 (or_5_out, and_3_out, and_4_out, and_5_out, and_6_out, and_7_out, and_8_out, and_8_out);
  or or_6 (or_6_out, and_12_out, and_13_out, and_16_out, and_14_out, and_15_out);
  or or_7 (or_7_out, and_1_out, and_32_out);
  or or_8 (or_8_out, and_17_out, and_18_out, and_19_out, and_20_out, and_21_out);
  or or_9 (or_9_out, and_22_out, and_23_out, and_24_out, and_25_out, and_26_out);
  or or_10 (or_10_out, and_27_out, and_28_out, and_29_out, and_30_out, and_31_out);
  _7_Segment_Display u_7_segment_display_1 (
    .g(or_10_out), .f(or_9_out), .a(or_5_out), .b(or_8_out), .e(or_7_out), .d(or_6_out), .c(or_4_out));  // open: dp
  xor xor_1 (xor_1_out, A0, B0);
  and and_33 (and_33_out, Cin, xor_1_out);
  and and_34 (and_34_out, A0, B0);
  LED led_1 (.in(or_24_out));
  _7_Segment_Display u_7_segment_display_2 (
    .g(or_21_out), .f(or_20_out), .a(or_19_out), .b(or_18_out), .e(or_22_out), .d(or_17_out), .c(or_15_out));  // open: dp
  LED led_2 (.in(xor_8_out));
  LED led_3 (.in(xor_6_out));
  xor xor_2 (xor_2_out, xor_1_out, Cin);
  or or_11 (or_11_out, and_33_out, and_34_out);
  LED led_4 (.in(xor_2_out));
  LED led_5 (.in(xor_4_out));
  or or_12 (or_12_out, in_3, not_3_out, A0);
  or or_13 (or_13_out, in_3, in_4);
  xor xor_3 (xor_3_out, in_4, in_8);
  and and_35 (and_35_out, or_11_out, xor_3_out);
  and and_36 (and_36_out, in_4, in_8);
  and and_37 (and_37_out, not_1_out, or_12_out);
  and and_38 (and_38_out, not_3_out, A0);
  and and_39 (and_39_out, A3, not_2_out);
  and and_40 (and_40_out, in_3, not_3_out, A0);
  and and_41 (and_41_out, in_3, in_4, not_4_out);
  and and_42 (and_42_out, not_1_out, not_2_out, not_4_out);
  and and_43 (and_43_out, not_2_out, in_4, A0);
  and and_44 (and_44_out, A3, not_3_out, not_4_out);
  and and_45 (and_45_out, or_13_out, A3);
  and and_46 (and_46_out, not_2_out, not_3_out);
  or or_14 (or_14_out, and_46_out, in_4);
  and and_47 (and_47_out, not_1_out, in_4);
  and and_48 (and_48_out, in_3, in_4);
  and and_49 (and_49_out, A3, not_4_out);
  and and_50 (and_50_out, not_1_out, in_3, A0);
  and and_51 (and_51_out, A3, not_2_out, not_3_out);
  and and_52 (and_52_out, not_2_out, not_3_out, not_4_out);
  _7_Segment_Display u_7_segment_display_3 (
    .g(in_10), .f(in_11), .a(in_12), .b(in_13), .e(in_14), .d(in_15), .c(in_16), .dp(in_17));
  or or_15 (or_15_out, and_37_out, and_38_out, and_39_out);
  and and_53 (and_53_out, or_14_out, not_4_out);
  and and_54 (and_54_out, not_1_out, not_2_out);
  and and_55 (and_55_out, not_1_out, not_3_out, not_4_out);
  and and_56 (and_56_out, not_1_out, in_4, A0);
  and and_57 (and_57_out, A3, not_3_out, A0);
  and and_58 (and_58_out, A3, not_2_out, not_4_out);
  and and_59 (and_59_out, not_3_out, not_4_out);
  and and_60 (and_60_out, A3, in_4);
  and and_61 (and_61_out, A3, not_2_out);
  and and_62 (and_62_out, not_1_out, in_3, not_3_out);
  and and_63 (and_63_out, in_3, in_4, not_4_out);
  and and_64 (and_64_out, in_4, not_4_out);
  and and_65 (and_65_out, A0, A3);
  and and_66 (and_66_out, A3, not_2_out);
  and and_67 (and_67_out, not_1_out, in_3, not_3_out);
  and and_68 (and_68_out, not_1_out, not_2_out, in_4);
  xor xor_4 (xor_4_out, xor_3_out, or_11_out);
  or or_16 (or_16_out, and_35_out, and_36_out);
  or or_17 (or_17_out, and_40_out, and_41_out, and_44_out, and_42_out, and_43_out);
  or or_18 (or_18_out, and_54_out, and_55_out, and_56_out, and_57_out, and_58_out);
  or or_19 (or_19_out, and_47_out, and_48_out, and_49_out, and_50_out, and_51_out, and_52_out, and_52_out);
  or or_20 (or_20_out, and_59_out, and_60_out, and_61_out, and_62_out, and_63_out);
  or or_21 (or_21_out, and_64_out, and_65_out, and_66_out, and_67_out, and_68_out);
  or or_22 (or_22_out, and_45_out, and_53_out);
  xor xor_5 (xor_5_out, in_3, in_7);
  and and_69 (and_69_out, or_16_out, xor_5_out);
  and and_70 (and_70_out, in_3, in_7);
  xor xor_6 (xor_6_out, xor_5_out, or_16_out);
  or or_23 (or_23_out, and_69_out, and_70_out);
  xor xor_7 (xor_7_out, A3, B3);
  and and_71 (and_71_out, or_23_out, xor_7_out);
  and and_72 (and_72_out, A3, B3);
  xor xor_8 (xor_8_out, xor_7_out, or_23_out);
  or or_24 (or_24_out, and_71_out, and_72_out);

  // Notes on the sheet:
  //   Num A
  //   Num B
  //   B0
  //   W
  //   W
  //   B2
  //   B1
  //   Y
  //   X
  //   Y
  //   X
  //   B3
  //   Z
  //   Z
  //   Z
  //   Y
  //   X
  //   W
  //   A
  //   B
  //   B0
  //   W
  //   W
  //   B2
  //   B1
  //   Y
  //   X
  //   X
  //   Sum
  //   Cout
  //   B3
  //   Z
  //   Y
  //   Z
  //   A
  //   B
  //   Cin
  //   Sum
  //   Cout
  //   A
  //   B
  //   Cin
  //   Sum
  //   Cout
  //   A
  //   B
  //   Cin
  //   Sum
  //   Cout
endmodule
