// Logisim project 8bitadder.circ as structural Verilog: 1 circuit, main circuit main
module main (
  input  A7,
  input  in_2,
  input  in_3,
  input  Cin,
  input  in_5,
  input  A3,
  input  in_7,
  input  in_8,
  input  A0,
  input  B7,
  input  in_11,
  input  in_12,
  input  in_13,
  input  B3,
  input  in_15,
  input  in_16,
  input  B0
);

  wire and_1_out, and_2_out, and_3_out, and_4_out, and_5_out, and_6_out, and_7_out, and_8_out, and_9_out,
       and_10_out, and_11_out, and_12_out, and_13_out, and_14_out, and_15_out, and_16_out, and_17_out,
       and_18_out, and_19_out, and_20_out, and_21_out, and_22_out, and_23_out, and_24_out, and_25_out,
       and_26_out, and_27_out, and_28_out, and_29_out, and_30_out, and_31_out, and_32_out, and_33_out,
       and_34_out, and_35_out, and_36_out, and_37_out, and_38_out, and_39_out, and_40_out, and_41_out,
       and_42_out, and_43_out, and_44_out, and_45_out, and_46_out, and_47_out, and_48_out, and_49_out,
       and_50_out, and_51_out, and_52_out, and_53_out, and_54_out, and_55_out, and_56_out, and_57_out,
       and_58_out, and_59_out, and_60_out, and_61_out, and_62_out, and_63_out, and_64_out, and_65_out,
       and_66_out, and_67_out, and_68_out, and_69_out, and_70_out, and_71_out, and_72_out, and_73_out,
       and_74_out, and_75_out, and_76_out, and_77_out, and_78_out, and_79_out, and_80_out, and_81_out,
       and_82_out, and_83_out, and_84_out, and_85_out, and_86_out, and_87_out, and_88_out, and_89_out,
       and_90_out, and_91_out, and_92_out, and_93_out, and_94_out, and_95_out, and_96_out, and_97_out,
       and_98_out, and_99_out, and_100_out, and_101_out, and_102_out, and_103_out, and_104_out, and_105_out,
       and_106_out, and_107_out, and_108_out, and_109_out, and_110_out, and_111_out, and_112_out,
       and_113_out, and_114_out, and_115_out, and_116_out, and_117_out, and_118_out, and_119_out,
       and_120_out, and_121_out, and_122_out, and_123_out, and_124_out, and_125_out, and_126_out,
       and_127_out, and_128_out, and_129_out, and_130_out, and_131_out, and_132_out, and_133_out,
       and_134_out, and_135_out, and_136_out, and_137_out, and_138_out, and_139_out, and_140_out,
       and_141_out, and_142_out, and_143_out, and_144_out, and_145_out, and_146_out, and_147_out,
       and_148_out, and_149_out, and_150_out, and_151_out, and_152_out, and_153_out, and_154_out,
       and_155_out, and_156_out, and_157_out, and_158_out, and_159_out, and_160_out, and_161_out,
       and_162_out, and_163_out, and_164_out, and_165_out, and_166_out, and_167_out, and_168_out,
       and_169_out, and_170_out, and_171_out, and_172_out, and_173_out, and_174_out, and_175_out,
       and_176_out, and_177_out, and_178_out, and_179_out, and_180_out, and_181_out, and_182_out,
       and_183_out, and_184_out, and_185_out, and_186_out, and_187_out, and_188_out, and_189_out,
       and_190_out, and_191_out, and_192_out, and_193_out, and_194_out, and_195_out, and_196_out,
       and_197_out, and_198_out, and_199_out, and_200_out, and_201_out, and_202_out, and_203_out,
       and_204_out, and_205_out, and_206_out, and_207_out, and_208_out, not_1_out, not_2_out, not_3_out,
       not_4_out, not_5_out, not_6_out, not_7_out, not_8_out, not_9_out, not_10_out, not_11_out, not_12_out,
       not_13_out, not_14_out, not_15_out, not_16_out, not_17_out, not_18_out, not_19_out, not_20_out,
       not_21_out, not_22_out, not_23_out, not_24_out, not_25_out, or_1_out, or_2_out, or_3_out, or_4_out,
       or_5_out, or_6_out, or_7_out, or_8_out, or_9_out, or_10_out, or_11_out, or_12_out, or_13_out,
       or_14_out, or_15_out, or_16_out, or_17_out, or_18_out, or_19_out, or_20_out, or_21_out, or_22_out,
       or_23_out, or_24_out, or_25_out, or_26_out, or_27_out, or_28_out, or_29_out, or_30_out, or_31_out,
       or_32_out, or_33_out, or_34_out, or_35_out, or_36_out, or_37_out, or_38_out, or_39_out, or_40_out,
       or_41_out, or_42_out, or_43_out, or_44_out, or_45_out, or_46_out, or_47_out, or_48_out, or_49_out,
       or_50_out, or_51_out, or_52_out, or_53_out, or_54_out, or_55_out, or_56_out, or_57_out, or_58_out,
       or_59_out, or_60_out, or_61_out, or_62_out, or_63_out, or_64_out, or_65_out, or_66_out, or_67_out,
       or_68_out, xor_1_out, xor_2_out, xor_3_out, xor_4_out, xor_5_out, xor_6_out, xor_7_out, xor_8_out,
       xor_9_out, xor_10_out, xor_11_out, xor_12_out, xor_13_out, xor_14_out, xor_15_out, xor_16_out;

  not not_1 (not_1_out, A3);
  not not_2 (not_2_out, in_7);
  not not_3 (not_3_out, in_8);
  not not_4 (not_4_out, A0);
  not not_5 (not_5_out, B3);
  not not_6 (not_6_out, in_15);
  not not_7 (not_7_out, in_16);
  not not_8 (not_8_out, B0);
  not not_9 (not_9_out, in_13);
  not not_10 (not_10_out, in_12);
  not not_11 (not_11_out, in_11);
  not not_12 (not_12_out, B7);
  or or_1 (or_1_out, in_15, in_16);
  or or_2 (or_2_out, in_11, in_12);
  or or_3 (or_3_out, in_15, not_7_out, B0);
  and and_1 (and_1_out, or_1_out, B3);
  and and_2 (and_2_out, not_6_out, not_7_out);
  and and_3 (and_3_out, not_5_out, in_16);
  and and_4 (and_4_out, in_15, in_16);
  and and_5 (and_5_out, B3, not_8_out);
  and and_6 (and_6_out, not_5_out, in_15, B0);
  and and_7 (and_7_out, B3, not_6_out, not_7_out);
  and and_8 (and_8_out, not_6_out, not_7_out, not_8_out);
  or or_4 (or_4_out, in_11, not_10_out, in_13);
  and and_9 (and_9_out, or_2_out, B7);
  and and_10 (and_10_out, not_11_out, not_10_out);
  and and_11 (and_11_out, not_12_out, in_12);
  and and_12 (and_12_out, in_11, in_12);
  and and_13 (and_13_out, B7, not_9_out);
  and and_14 (and_14_out, not_12_out, in_11, in_13);
  and and_15 (and_15_out, B7, not_11_out, not_10_out);
  and and_16 (and_16_out, not_11_out, not_10_out, not_9_out);
  and and_17 (and_17_out, not_5_out, or_3_out);
  and and_18 (and_18_out, not_7_out, B0);
  and and_19 (and_19_out, B3, not_6_out);
  and and_20 (and_20_out, in_15, not_7_out, B0);
  and and_21 (and_21_out, in_15, in_16, not_8_out);
  and and_22 (and_22_out, not_5_out, not_6_out, not_8_out);
  and and_23 (and_23_out, not_6_out, in_16, B0);
  and and_24 (and_24_out, B3, not_7_out, not_8_out);
  or or_5 (or_5_out, and_2_out, in_16);
  and and_25 (and_25_out, not_5_out, not_6_out);
  and and_26 (and_26_out, not_5_out, not_7_out, not_8_out);
  and and_27 (and_27_out, not_5_out, in_16, B0);
  and and_28 (and_28_out, B3, not_7_out, B0);
  and and_29 (and_29_out, B3, not_6_out, not_8_out);
  and and_30 (and_30_out, not_7_out, not_8_out);
  and and_31 (and_31_out, B3, in_16);
  and and_32 (and_32_out, B3, not_6_out);
  and and_33 (and_33_out, not_5_out, in_15, not_7_out);
  and and_34 (and_34_out, in_15, in_16, not_8_out);
  and and_35 (and_35_out, in_16, not_8_out);
  and and_36 (and_36_out, B0, B3);
  and and_37 (and_37_out, B3, not_6_out);
  and and_38 (and_38_out, not_5_out, in_15, not_7_out);
  and and_39 (and_39_out, not_5_out, not_6_out, in_16);
  and and_40 (and_40_out, not_12_out, or_4_out);
  and and_41 (and_41_out, not_10_out, in_13);
  and and_42 (and_42_out, B7, not_11_out);
  and and_43 (and_43_out, in_11, not_10_out, in_13);
  and and_44 (and_44_out, in_11, in_12, not_9_out);
  and and_45 (and_45_out, not_12_out, not_11_out, not_9_out);
  and and_46 (and_46_out, not_11_out, in_12, in_13);
  and and_47 (and_47_out, B7, not_10_out, not_9_out);
  or or_6 (or_6_out, and_10_out, in_12);
  and and_48 (and_48_out, not_12_out, not_11_out);
  and and_49 (and_49_out, not_12_out, not_10_out, not_9_out);
  and and_50 (and_50_out, not_12_out, in_12, in_13);
  and and_51 (and_51_out, B7, not_10_out, in_13);
  and and_52 (and_52_out, B7, not_11_out, not_9_out);
  and and_53 (and_53_out, not_10_out, not_9_out);
  and and_54 (and_54_out, B7, in_12);
  and and_55 (and_55_out, B7, not_11_out);
  and and_56 (and_56_out, not_12_out, in_11, not_10_out);
  and and_57 (and_57_out, in_11, in_12, not_9_out);
  and and_58 (and_58_out, in_12, not_9_out);
  and and_59 (and_59_out, in_13, B7);
  and and_60 (and_60_out, B7, not_11_out);
  and and_61 (and_61_out, not_12_out, in_11, not_10_out);
  and and_62 (and_62_out, not_12_out, not_11_out, in_12);
  or or_7 (or_7_out, and_17_out, and_18_out, and_19_out);
  and and_63 (and_63_out, or_5_out, not_8_out);
  or or_8 (or_8_out, and_3_out, and_4_out, and_5_out, and_6_out, and_7_out, and_8_out, and_8_out);
  or or_9 (or_9_out, and_40_out, and_41_out, and_42_out);
  and and_64 (and_64_out, or_6_out, not_9_out);
  or or_10 (or_10_out, and_11_out, and_12_out, and_13_out, and_14_out, and_15_out, and_16_out, and_16_out);
  or or_11 (or_11_out, and_20_out, and_21_out, and_24_out, and_22_out, and_23_out);
  or or_12 (or_12_out, and_1_out, and_63_out);
  or or_13 (or_13_out, and_25_out, and_26_out, and_27_out, and_28_out, and_29_out);
  or or_14 (or_14_out, and_30_out, and_31_out, and_32_out, and_33_out, and_34_out);
  or or_15 (or_15_out, and_35_out, and_36_out, and_37_out, and_38_out, and_39_out);
  or or_16 (or_16_out, and_43_out, and_44_out, and_47_out, and_45_out, and_46_out);
  or or_17 (or_17_out, and_9_out, and_64_out);
  or or_18 (or_18_out, and_48_out, and_49_out, and_50_out, and_51_out, and_52_out);
  or or_19 (or_19_out, and_53_out, and_54_out, and_55_out, and_56_out, and_57_out);
  or or_20 (or_20_out, and_58_out, and_59_out, and_60_out, and_61_out, and_62_out);
  _7_Segment_Display u_7_segment_display_1 (
    .g(or_20_out), .f(or_19_out), .a(or_10_out), .b(or_18_out), .e(or_17_out), .d(or_16_out), .c(or_9_out));  // open: dp
  _7_Segment_Display u_7_segment_display_2 (
    .g(or_34_out), .f(or_33_out), .a(or_32_out), .b(or_31_out), .e(or_41_out), .d(or_30_out), .c(or_28_out));  // open: dp
  _7_Segment_Display u_7_segment_display_3 (
    .g(or_15_out), .f(or_14_out), .a(or_8_out), .b(or_13_out), .e(or_12_out), .d(or_11_out), .c(or_7_out));  // open: dp
  xor xor_1 (xor_1_out, A0, B0);
  and and_65 (and_65_out, Cin, xor_1_out);
  and and_66 (and_66_out, A0, B0);
  _7_Segment_Display u_7_segment_display_4 (
    .g(or_40_out), .f(or_39_out), .a(or_38_out), .b(or_37_out), .e(or_42_out), .d(or_36_out), .c(or_29_out));  // open: dp
  LED led_1 (.in(or_46_out));
  not not_13 (not_13_out, A7);
  not not_14 (not_14_out, in_2);
  LED led_2 (.in(xor_6_out));
  LED led_3 (.in(xor_8_out));
  not not_15 (not_15_out, in_5);
  not not_16 (not_16_out, in_3);
  xor xor_2 (xor_2_out, xor_1_out, Cin);
  or or_21 (or_21_out, and_65_out, and_66_out);
  LED led_4 (.in(xor_4_out));
  LED led_5 (.in(xor_2_out));
  _7_Segment_Display u_7_segment_display_5 (
    .f(not_21_out), .a(not_21_out), .b(1'b1), .e(not_21_out), .d(not_21_out), .c(1'b1));  // open: g, dp
  _7_Segment_Display u_7_segment_display_6 (
    .g(or_54_out), .f(or_53_out), .a(or_51_out), .b(or_50_out), .e(or_52_out), .d(or_49_out), .c(or_47_out));  // open: dp
  _7_Segment_Display u_7_segment_display_7 (
    .g(or_66_out), .f(or_65_out), .a(or_63_out), .b(or_62_out), .e(or_64_out), .d(or_61_out), .c(or_60_out));  // open: dp
  or or_22 (or_22_out, in_2, not_16_out, in_5);
  or or_23 (or_23_out, in_2, in_3);
  or or_24 (or_24_out, in_7, not_3_out, A0);
  or or_25 (or_25_out, in_7, in_8);
  and and_67 (and_67_out, not_13_out, or_22_out);
  and and_68 (and_68_out, not_16_out, in_5);
  and and_69 (and_69_out, A7, not_14_out);
  and and_70 (and_70_out, in_2, not_16_out, in_5);
  and and_71 (and_71_out, in_2, in_3, not_15_out);
  and and_72 (and_72_out, not_13_out, not_14_out, not_15_out);
  and and_73 (and_73_out, not_14_out, in_3, in_5);
  and and_74 (and_74_out, A7, not_16_out, not_15_out);
  and and_75 (and_75_out, or_23_out, A7);
  and and_76 (and_76_out, not_14_out, not_16_out);
  or or_26 (or_26_out, and_76_out, in_3);
  and and_77 (and_77_out, not_13_out, in_3);
  and and_78 (and_78_out, in_2, in_3);
  and and_79 (and_79_out, A7, not_15_out);
  and and_80 (and_80_out, not_13_out, in_2, in_5);
  and and_81 (and_81_out, A7, not_14_out, not_16_out);
  and and_82 (and_82_out, not_14_out, not_16_out, not_15_out);
  xor xor_3 (xor_3_out, in_8, in_16);
  and and_83 (and_83_out, or_21_out, xor_3_out);
  and and_84 (and_84_out, in_8, in_16);
  and and_85 (and_85_out, not_1_out, or_24_out);
  and and_86 (and_86_out, not_3_out, A0);
  and and_87 (and_87_out, A3, not_2_out);
  and and_88 (and_88_out, in_7, not_3_out, A0);
  and and_89 (and_89_out, in_7, in_8, not_4_out);
  and and_90 (and_90_out, not_1_out, not_2_out, not_4_out);
  and and_91 (and_91_out, not_2_out, in_8, A0);
  and and_92 (and_92_out, A3, not_3_out, not_4_out);
  and and_93 (and_93_out, or_25_out, A3);
  and and_94 (and_94_out, not_2_out, not_3_out);
  or or_27 (or_27_out, and_94_out, in_8);
  and and_95 (and_95_out, not_1_out, in_8);
  and and_96 (and_96_out, in_7, in_8);
  and and_97 (and_97_out, A3, not_4_out);
  and and_98 (and_98_out, not_1_out, in_7, A0);
  and and_99 (and_99_out, A3, not_2_out, not_3_out);
  and and_100 (and_100_out, not_2_out, not_3_out, not_4_out);
  or or_28 (or_28_out, and_67_out, and_68_out, and_69_out);
  and and_101 (and_101_out, or_26_out, not_15_out);
  and and_102 (and_102_out, not_13_out, not_14_out);
  and and_103 (and_103_out, not_13_out, not_16_out, not_15_out);
  and and_104 (and_104_out, not_13_out, in_3, in_5);
  and and_105 (and_105_out, A7, not_16_out, in_5);
  and and_106 (and_106_out, A7, not_14_out, not_15_out);
  and and_107 (and_107_out, not_16_out, not_15_out);
  and and_108 (and_108_out, A7, in_3);
  and and_109 (and_109_out, A7, not_14_out);
  and and_110 (and_110_out, not_13_out, in_2, not_16_out);
  and and_111 (and_111_out, in_2, in_3, not_15_out);
  and and_112 (and_112_out, in_3, not_15_out);
  and and_113 (and_113_out, in_5, A7);
  and and_114 (and_114_out, A7, not_14_out);
  and and_115 (and_115_out, not_13_out, in_2, not_16_out);
  and and_116 (and_116_out, not_13_out, not_14_out, in_3);
  or or_29 (or_29_out, and_85_out, and_86_out, and_87_out);
  and and_117 (and_117_out, or_27_out, not_4_out);
  and and_118 (and_118_out, not_1_out, not_2_out);
  and and_119 (and_119_out, not_1_out, not_3_out, not_4_out);
  and and_120 (and_120_out, not_1_out, in_8, A0);
  and and_121 (and_121_out, A3, not_3_out, A0);
  and and_122 (and_122_out, A3, not_2_out, not_4_out);
  and and_123 (and_123_out, not_3_out, not_4_out);
  and and_124 (and_124_out, A3, in_8);
  and and_125 (and_125_out, A3, not_2_out);
  and and_126 (and_126_out, not_1_out, in_7, not_3_out);
  and and_127 (and_127_out, in_7, in_8, not_4_out);
  and and_128 (and_128_out, in_8, not_4_out);
  and and_129 (and_129_out, A0, A3);
  and and_130 (and_130_out, A3, not_2_out);
  and and_131 (and_131_out, not_1_out, in_7, not_3_out);
  and and_132 (and_132_out, not_1_out, not_2_out, in_8);
  or or_30 (or_30_out, and_70_out, and_71_out, and_74_out, and_72_out, and_73_out);
  or or_31 (or_31_out, and_102_out, and_103_out, and_104_out, and_105_out, and_106_out);
  or or_32 (or_32_out, and_77_out, and_78_out, and_79_out, and_80_out, and_81_out, and_82_out, and_82_out);
  or or_33 (or_33_out, and_107_out, and_108_out, and_109_out, and_110_out, and_111_out);
  or or_34 (or_34_out, and_112_out, and_113_out, and_114_out, and_115_out, and_116_out);
  xor xor_4 (xor_4_out, xor_3_out, or_21_out);
  or or_35 (or_35_out, and_83_out, and_84_out);
  or or_36 (or_36_out, and_88_out, and_89_out, and_92_out, and_90_out, and_91_out);
  or or_37 (or_37_out, and_118_out, and_119_out, and_120_out, and_121_out, and_122_out);
  or or_38 (or_38_out, and_95_out, and_96_out, and_97_out, and_98_out, and_99_out, and_100_out, and_100_out);
  or or_39 (or_39_out, and_123_out, and_124_out, and_125_out, and_126_out, and_127_out);
  or or_40 (or_40_out, and_128_out, and_129_out, and_130_out, and_131_out, and_132_out);
  or or_41 (or_41_out, and_75_out, and_101_out);
  or or_42 (or_42_out, and_93_out, and_117_out);
  xor xor_5 (xor_5_out, in_7, in_15);
  and and_133 (and_133_out, or_35_out, xor_5_out);
  and and_134 (and_134_out, in_7, in_15);
  xor xor_6 (xor_6_out, xor_5_out, or_35_out);
  or or_43 (or_43_out, and_133_out, and_134_out);
  not not_17 (not_17_out, xor_8_out);
  not not_18 (not_18_out, xor_6_out);
  not not_19 (not_19_out, xor_4_out);
  not not_20 (not_20_out, xor_2_out);
  xor xor_7 (xor_7_out, A3, B3);
  not not_21 (not_21_out, or_68_out);
  and and_135 (and_135_out, or_43_out, xor_7_out);
  and and_136 (and_136_out, A3, B3);
  or or_44 (or_44_out, xor_6_out, not_19_out, xor_2_out);
  or or_45 (or_45_out, xor_6_out, xor_4_out);
  and and_137 (and_137_out, not_17_out, or_44_out);
  and and_138 (and_138_out, not_19_out, xor_2_out);
  and and_139 (and_139_out, xor_8_out, not_18_out);
  and and_140 (and_140_out, xor_6_out, not_19_out, xor_2_out);
  and and_141 (and_141_out, xor_6_out, xor_4_out, not_20_out);
  and and_142 (and_142_out, not_17_out, not_18_out, not_20_out);
  and and_143 (and_143_out, not_18_out, xor_4_out, xor_2_out);
  and and_144 (and_144_out, xor_8_out, not_19_out, not_20_out);
  and and_145 (and_145_out, or_45_out, xor_8_out);
  and and_146 (and_146_out, not_18_out, not_19_out);
  and and_147 (and_147_out, not_17_out, xor_4_out);
  and and_148 (and_148_out, xor_6_out, xor_4_out);
  and and_149 (and_149_out, xor_8_out, not_20_out);
  and and_150 (and_150_out, not_17_out, xor_6_out, xor_2_out);
  and and_151 (and_151_out, xor_8_out, not_18_out, not_19_out);
  and and_152 (and_152_out, not_18_out, not_19_out, not_20_out);
  xor xor_8 (xor_8_out, xor_7_out, or_43_out);
  or or_46 (or_46_out, and_135_out, and_136_out);
  or or_47 (or_47_out, and_137_out, and_138_out, and_139_out);
  or or_48 (or_48_out, and_146_out, xor_4_out);
  and and_153 (and_153_out, or_48_out, not_20_out);
  and and_154 (and_154_out, not_17_out, not_18_out);
  and and_155 (and_155_out, not_17_out, not_19_out, not_20_out);
  and and_156 (and_156_out, not_17_out, xor_4_out, xor_2_out);
  and and_157 (and_157_out, xor_8_out, not_19_out, xor_2_out);
  and and_158 (and_158_out, xor_8_out, not_18_out, not_20_out);
  and and_159 (and_159_out, not_19_out, not_20_out);
  and and_160 (and_160_out, xor_8_out, xor_4_out);
  and and_161 (and_161_out, xor_8_out, not_18_out);
  and and_162 (and_162_out, not_17_out, xor_6_out, not_19_out);
  and and_163 (and_163_out, xor_6_out, xor_4_out, not_20_out);
  and and_164 (and_164_out, xor_4_out, not_20_out);
  and and_165 (and_165_out, xor_2_out, xor_8_out);
  and and_166 (and_166_out, xor_8_out, not_18_out);
  and and_167 (and_167_out, not_17_out, xor_6_out, not_19_out);
  and and_168 (and_168_out, not_17_out, not_18_out, xor_4_out);
  or or_49 (or_49_out, and_140_out, and_141_out, and_144_out, and_142_out, and_143_out);
  or or_50 (or_50_out, and_154_out, and_155_out, and_156_out, and_157_out, and_158_out);
  or or_51 (or_51_out, and_147_out, and_148_out, and_149_out, and_150_out, and_151_out, and_152_out, and_152_out);
  xor xor_9 (xor_9_out, A7, B7);
  or or_52 (or_52_out, and_145_out, and_153_out);
  or or_53 (or_53_out, and_159_out, and_160_out, and_161_out, and_162_out, and_163_out);
  or or_54 (or_54_out, and_164_out, and_165_out, and_166_out, and_167_out, and_168_out);
  and and_169 (and_169_out, or_46_out, xor_9_out);
  and and_170 (and_170_out, A7, B7);
  xor xor_10 (xor_10_out, xor_9_out, or_46_out);
  or or_55 (or_55_out, and_169_out, and_170_out);
  not not_22 (not_22_out, xor_16_out);
  not not_23 (not_23_out, xor_12_out);
  not not_24 (not_24_out, xor_14_out);
  xor xor_11 (xor_11_out, in_2, in_11);
  not not_25 (not_25_out, xor_10_out);
  and and_171 (and_171_out, or_55_out, xor_11_out);
  and and_172 (and_172_out, in_2, in_11);
  or or_56 (or_56_out, xor_14_out, not_23_out, xor_10_out);
  or or_57 (or_57_out, xor_14_out, xor_12_out);
  xor xor_12 (xor_12_out, xor_11_out, or_55_out);
  or or_58 (or_58_out, and_171_out, and_172_out);
  and and_173 (and_173_out, not_22_out, or_56_out);
  and and_174 (and_174_out, not_23_out, xor_10_out);
  and and_175 (and_175_out, xor_16_out, not_24_out);
  and and_176 (and_176_out, xor_14_out, not_23_out, xor_10_out);
  and and_177 (and_177_out, xor_14_out, xor_12_out, not_25_out);
  and and_178 (and_178_out, not_22_out, not_24_out, not_25_out);
  and and_179 (and_179_out, not_24_out, xor_12_out, xor_10_out);
  and and_180 (and_180_out, xor_16_out, not_23_out, not_25_out);
  and and_181 (and_181_out, or_57_out, xor_16_out);
  and and_182 (and_182_out, not_24_out, not_23_out);
  and and_183 (and_183_out, not_22_out, xor_12_out);
  and and_184 (and_184_out, xor_14_out, xor_12_out);
  and and_185 (and_185_out, xor_16_out, not_25_out);
  and and_186 (and_186_out, not_22_out, xor_14_out, xor_10_out);
  and and_187 (and_187_out, xor_16_out, not_24_out, not_23_out);
  and and_188 (and_188_out, not_24_out, not_23_out, not_25_out);
  or or_59 (or_59_out, and_182_out, xor_12_out);
  and and_189 (and_189_out, not_22_out, not_24_out);
  and and_190 (and_190_out, not_22_out, not_23_out, not_25_out);
  and and_191 (and_191_out, not_22_out, xor_12_out, xor_10_out);
  and and_192 (and_192_out, xor_16_out, not_23_out, xor_10_out);
  and and_193 (and_193_out, xor_16_out, not_24_out, not_25_out);
  and and_194 (and_194_out, not_23_out, not_25_out);
  and and_195 (and_195_out, xor_16_out, xor_12_out);
  and and_196 (and_196_out, xor_16_out, not_24_out);
  and and_197 (and_197_out, not_22_out, xor_14_out, not_23_out);
  and and_198 (and_198_out, xor_14_out, xor_12_out, not_25_out);
  and and_199 (and_199_out, xor_12_out, not_25_out);
  and and_200 (and_200_out, xor_10_out, xor_16_out);
  and and_201 (and_201_out, xor_16_out, not_24_out);
  and and_202 (and_202_out, not_22_out, xor_14_out, not_23_out);
  and and_203 (and_203_out, not_22_out, not_24_out, xor_12_out);
  xor xor_13 (xor_13_out, in_3, in_12);
  or or_60 (or_60_out, and_173_out, and_174_out, and_175_out);
  or or_61 (or_61_out, and_176_out, and_177_out, and_180_out, and_178_out, and_179_out);
  and and_204 (and_204_out, or_59_out, not_25_out);
  or or_62 (or_62_out, and_189_out, and_190_out, and_191_out, and_192_out, and_193_out);
  or or_63 (or_63_out, and_183_out, and_184_out, and_185_out, and_186_out, and_187_out, and_188_out, and_188_out);
  and and_205 (and_205_out, or_58_out, xor_13_out);
  and and_206 (and_206_out, in_3, in_12);
  or or_64 (or_64_out, and_181_out, and_204_out);
  or or_65 (or_65_out, and_194_out, and_195_out, and_196_out, and_197_out, and_198_out);
  or or_66 (or_66_out, and_199_out, and_200_out, and_201_out, and_202_out, and_203_out);
  xor xor_14 (xor_14_out, xor_13_out, or_58_out);
  or or_67 (or_67_out, and_205_out, and_206_out);
  xor xor_15 (xor_15_out, in_5, in_13);
  and and_207 (and_207_out, or_67_out, xor_15_out);
  and and_208 (and_208_out, in_5, in_13);
  xor xor_16 (xor_16_out, xor_15_out, or_67_out);
  or or_68 (or_68_out, and_207_out, and_208_out);

  // Notes on the sheet:
  //   Num A
  //   Num B
  //   B0
  //   W
  //   W
  //   B0
  //   W
  //   W
  //   B2
  //   B1
  //   Y
  //   X
  //   X
  //   Y
  //   B2
  //   B1
  //   Y
  //   X
  //   Y
  //   X
  //   B3
  //   Z
  //   Z
  //   B3
  //   Z
  //   Z
  //   Num B display Logic (B6 top-B0 bottom)
  //   Z
  //   Y
  //   X
  //   W
  //   A
  //   B
  //   B0
  //   W
  //   W
  //   B0
  //   W
  //   W
  //   B2
  //   B1
  //   Y
  //   X
  //   X
  //   B2
  //   B1
  //   Y
  //   X
  //   X
  //   B3
  //   Z
  //   Y
  //   Z
  //   Sum
  //   Cout
  //   B3
  //   Z
  //   Y
  //   Z
  //   A
  //   B
  //   Cin
  //   Num A display Logic (A6 top-A0 bottom)
  //   Result first digit display Logic (S6 top-S0 bottom)
  //   Sum
  //   Cout
  //   A
  //   B
  //   Cin
  //   W
  //   Sum
  //   Cout
  //   B0
  //   B1
  //   X
  //   X
  //   W
  //   A
  //   B
  //   Cin
  //   B2
  //   B3
  //   Z
  //   Y
  //   Y
  //   Z
  //   Result first digit display Logic (S6 top-S0 bottom)
  //   Sum
  //   Cout
  //   A
  //   B
  //   Cin
  //   Sum
  //   A
  //   B
  //   Cin
  //   Cout
  //   B0
  //   B1
  //   X
  //   W
  //   X
  //   W
  //   B2
  //   B3
  //   Z
  //   Y
  //   Y
  //   Z
  //   Result first digit display Logic (S6 top-S0 bottom)
  //   Sum
  //   Cout
  //   A
  //   B
  //   Cin
  //   Sum
  //   Cout
  //   A
  //   B
  //   Cin
  //   Sum
  //   Cout
endmodule
