// Logisim project BenEaterPC.circ as structural Verilog: 8 circuits, main circuit main
module main (
  input  in_1,
  input  in_2,
  input  in_3,
  input  in_4,
  input  in_5,
  input  in_6,
  input  in_7,
  input  in_8,
  input  in_9,
  input  in_10,
  input  in_11,
  input  Aout,
  input  Ain,
  input  Bout,
  input  Bin,
  input  SumOut,
  input  SumIn,
  input  Subtraction,
  input  A2S,
  input  B2S,
  input  PCout,
  input  MARin,
  input  MARout,
  input  IPin,
  input  IPout,
  input  RAM_read,
  input  Value_to_Bus
);

  wire clock_1_out, controlled_buffer_8_out, controlled_buffer_9_out, controlled_buffer_12_out,
       controlled_buffer_13_out, controlled_buffer_14_out, controlled_buffer_15_out,
       controlled_buffer_16_out, controlled_buffer_17_out, controlled_buffer_18_out,
       controlled_buffer_19_out, controlled_buffer_20_out, controlled_buffer_21_out,
       controlled_buffer_22_out, controlled_buffer_23_out, controlled_buffer_24_out,
       controlled_buffer_25_out, n4bitadder_1_cout, n4bitadder_2_cout, n7segencoder_1_out_5,
       n7segencoder_1_out_6, n7segencoder_1_out_7, n7segencoder_1_out_8, n7segencoder_1_out_9,
       n7segencoder_1_out_10, n7segencoder_1_out_11, n7segencoder_2_out_5, n7segencoder_2_out_6,
       n7segencoder_2_out_7, n7segencoder_2_out_8, n7segencoder_2_out_9, n7segencoder_2_out_10,
       n7segencoder_2_out_11, n7segencoder_3_out_5, n7segencoder_3_out_6, n7segencoder_3_out_7,
       n7segencoder_3_out_8, n7segencoder_3_out_9, n7segencoder_3_out_10, n7segencoder_3_out_11,
       n7segencoder_4_out_5, n7segencoder_4_out_6, n7segencoder_4_out_7, n7segencoder_4_out_8,
       n7segencoder_4_out_9, n7segencoder_4_out_10, n7segencoder_4_out_11, not_1_out, not_2_out, xor_1_out,
       xor_2_out, xor_3_out, xor_4_out, xor_5_out, xor_6_out, xor_7_out, xor_8_out;
  wire [2:0] carrybit_1__6, n7segencoder_5_out_5, n7segencoder_6_out_5;
  wire [3:0] carrybit_1__3, n4bitadder_1_sum, n4bitadder_2_sum, n4bitregister_1_out_8, n7segencoder_5_out_8,
       n7segencoder_6_out_8, register_3_out_11, register_3_out_15;
  wire [7:0] controlled_buffer_1_out, controlled_buffer_10_out, controlled_buffer_11_out, counter_1_q,
       n4bitregister_2_out_8, register_1_out_11, register_2_out_11;

  Button button_1 (.out(n4bitregister_2_out_8[7]));
  LED led_1 (.in(Aout));
  LED led_2 (.in(Ain));
  LED led_3 (.in(Bout));
  LED led_4 (.in(Bin));
  LED led_5 (.in(SumOut));
  LED led_6 (.in(SumIn));
  LED led_7 (.in(Subtraction));
  LED led_8 (.in(A2S));
  LED led_9 (.in(B2S));
  LED led_10 (.in(PCout));
  LED led_11 (.in(MARin));
  LED led_12 (.in(MARout));
  LED led_13 (.in(IPin));
  LED led_14 (.in(IPout));
  LED led_15 (.in(not_1_out));
  LED led_16 (.in(RAM_read));
  LED led_17 (.in(Value_to_Bus));
  _4bitRegister u_4bitregister_1 (
    .Clk(clock_1_out), .En(MARin), .D(controlled_buffer_1_out[0]), .D_2(controlled_buffer_1_out[1]),
    .D_3(controlled_buffer_1_out[2]), .D_4(controlled_buffer_1_out[3]), .out_8(n4bitregister_1_out_8[0]),
    .in_4(n4bitregister_2_out_8[7]), .out_9(n4bitregister_1_out_8[1]), .out_10(n4bitregister_1_out_8[2]),
    .out_11(n4bitregister_1_out_8[3]));
  _4bitRegister u_4bitregister_2 (
    .Clk(clock_1_out), .En(IPin), .D(controlled_buffer_1_out[4]), .D_2(controlled_buffer_1_out[5]),
    .D_3(controlled_buffer_1_out[6]), .D_4(controlled_buffer_1_out[7]), .out_8(n4bitregister_2_out_8[0]),
    .in_4(n4bitregister_2_out_8[7]), .out_9(n4bitregister_2_out_8[1]), .out_10(n4bitregister_2_out_8[2]),
    .out_11(n4bitregister_2_out_8[3]));
  assign controlled_buffer_1_out = IPout ? {{4{n4bitregister_2_out_8[7]}}, n4bitregister_2_out_8[3:0]} : 8'bz;  // Controlled_Buffer controlled_buffer_1
  not not_1 (not_1_out, not_2_out);
  assign controlled_buffer_1_out = Value_to_Bus ? {in_4, in_5, in_6, in_7, in_8, in_9, in_10, in_11} : 8'bz;  // Controlled_Buffer controlled_buffer_2
  assign controlled_buffer_1_out = Aout ? register_1_out_11 : 8'bz;  // Controlled_Buffer controlled_buffer_3
  assign controlled_buffer_1_out = Bout ? register_2_out_11 : 8'bz;  // Controlled_Buffer controlled_buffer_4
  Clock clock_1 (.out(clock_1_out));
  assign controlled_buffer_1_out = SumOut ? {register_3_out_15, register_3_out_11} : 8'bz;  // Controlled_Buffer controlled_buffer_5
  Counter counter_1 (
    .load(in_2), .D(controlled_buffer_1_out), .count(in_3), .Q(counter_1_q), .clk(clock_1_out),
    .clr(n4bitregister_2_out_8[7]));  // open: carry
  xor xor_1 (xor_1_out, controlled_buffer_17_out, Subtraction);
  assign controlled_buffer_1_out = in_1 ? controlled_buffer_10_out : 8'bz;  // Controlled_Buffer controlled_buffer_6
  assign controlled_buffer_1_out = PCout ? counter_1_q : 8'bz;  // Controlled_Buffer controlled_buffer_7
  assign controlled_buffer_8_out = B2S ? register_1_out_11[1] : 1'bz;  // Controlled_Buffer controlled_buffer_8
  assign controlled_buffer_9_out = B2S ? register_1_out_11[0] : 1'bz;  // Controlled_Buffer controlled_buffer_9
  xor xor_2 (xor_2_out, controlled_buffer_18_out, Subtraction);
  assign controlled_buffer_10_out = MARout ? {{4{n4bitregister_2_out_8[7]}}, n4bitregister_1_out_8} : 8'bz;  // Controlled_Buffer controlled_buffer_10
  assign controlled_buffer_11_out = RAM_read ? controlled_buffer_1_out : 8'bz;  // Controlled_Buffer controlled_buffer_11
  assign controlled_buffer_12_out = B2S ? register_1_out_11[3] : 1'bz;  // Controlled_Buffer controlled_buffer_12
  assign controlled_buffer_13_out = B2S ? register_1_out_11[5] : 1'bz;  // Controlled_Buffer controlled_buffer_13
  assign controlled_buffer_14_out = B2S ? register_1_out_11[4] : 1'bz;  // Controlled_Buffer controlled_buffer_14
  assign controlled_buffer_15_out = B2S ? register_1_out_11[2] : 1'bz;  // Controlled_Buffer controlled_buffer_15
  xor xor_3 (xor_3_out, controlled_buffer_16_out, Subtraction);
  xor xor_4 (xor_4_out, controlled_buffer_24_out, Subtraction);
  assign controlled_buffer_16_out = A2S ? register_2_out_11[2] : 1'bz;  // Controlled_Buffer controlled_buffer_16
  assign controlled_buffer_17_out = A2S ? register_2_out_11[0] : 1'bz;  // Controlled_Buffer controlled_buffer_17
  assign controlled_buffer_18_out = A2S ? register_2_out_11[1] : 1'bz;  // Controlled_Buffer controlled_buffer_18
  not not_2 (not_2_out, MARout);
  assign controlled_buffer_19_out = B2S ? register_1_out_11[6] : 1'bz;  // Controlled_Buffer controlled_buffer_19
  assign controlled_buffer_20_out = B2S ? register_1_out_11[7] : 1'bz;  // Controlled_Buffer controlled_buffer_20
  xor xor_5 (xor_5_out, controlled_buffer_23_out, Subtraction);
  assign controlled_buffer_21_out = A2S ? register_2_out_11[5] : 1'bz;  // Controlled_Buffer controlled_buffer_21
  assign controlled_buffer_22_out = A2S ? register_2_out_11[6] : 1'bz;  // Controlled_Buffer controlled_buffer_22
  assign controlled_buffer_23_out = A2S ? register_2_out_11[4] : 1'bz;  // Controlled_Buffer controlled_buffer_23
  assign controlled_buffer_24_out = A2S ? register_2_out_11[3] : 1'bz;  // Controlled_Buffer controlled_buffer_24
  RAM_part #(.bus("asynch")) ram_1 (
    .addr(controlled_buffer_11_out), .data(controlled_buffer_10_out), .ld(not_2_out),
    .clr(n4bitregister_2_out_8[7]));  // open: sel
  Register register_1 (
    .Clk(clock_1_out), .En(Ain), .D(controlled_buffer_1_out[0]), .D_2(controlled_buffer_1_out[1]),
    .D_3(controlled_buffer_1_out[2]), .D_4(controlled_buffer_1_out[3]), .D_5(controlled_buffer_1_out[4]),
    .D_6(controlled_buffer_1_out[5]), .D_7(controlled_buffer_1_out[6]), .D_8(controlled_buffer_1_out[7]),
    .out_11(register_1_out_11[0]), .out_12(register_1_out_11[1]), .out_13(register_1_out_11[2]),
    .out_14(register_1_out_11[3]), .out_15(register_1_out_11[4]), .out_16(register_1_out_11[5]),
    .out_17(register_1_out_11[6]), .out_18(register_1_out_11[7]));
  xor xor_6 (xor_6_out, controlled_buffer_21_out, Subtraction);
  assign controlled_buffer_25_out = A2S ? register_2_out_11[7] : 1'bz;  // Controlled_Buffer controlled_buffer_25
  Register register_2 (
    .Clk(clock_1_out), .En(Bin), .D(controlled_buffer_1_out[0]), .D_2(controlled_buffer_1_out[1]),
    .D_3(controlled_buffer_1_out[2]), .D_4(controlled_buffer_1_out[3]), .D_5(controlled_buffer_1_out[4]),
    .D_6(controlled_buffer_1_out[5]), .D_7(controlled_buffer_1_out[6]), .D_8(controlled_buffer_1_out[7]),
    .out_11(register_2_out_11[0]), .out_12(register_2_out_11[1]), .out_13(register_2_out_11[2]),
    .out_14(register_2_out_11[3]), .out_15(register_2_out_11[4]), .out_16(register_2_out_11[5]),
    .out_17(register_2_out_11[6]), .out_18(register_2_out_11[7]));
  xor xor_7 (xor_7_out, controlled_buffer_22_out, Subtraction);
  xor xor_8 (xor_8_out, controlled_buffer_25_out, Subtraction);
  _4bitadder u_4bitadder_1 (
    .in_1(controlled_buffer_9_out), .in_2(controlled_buffer_8_out), .in_3(controlled_buffer_15_out),
    .in_4(controlled_buffer_12_out), .in_5(xor_1_out), .in_6(xor_2_out), .in_7(xor_3_out), .in_8(xor_4_out),
    .in_9(Subtraction), .Sum(n4bitadder_1_sum[0]), .Sum_2(n4bitadder_1_sum[1]), .Sum_3(n4bitadder_1_sum[2]),
    .Sum_4(n4bitadder_1_sum[3]), .Cout(n4bitadder_1_cout));
  _4bitadder u_4bitadder_2 (
    .in_1(controlled_buffer_14_out), .in_2(controlled_buffer_13_out), .in_3(controlled_buffer_19_out),
    .in_4(controlled_buffer_20_out), .in_5(xor_5_out), .in_6(xor_6_out), .in_7(xor_7_out), .in_8(xor_8_out),
    .in_9(n4bitadder_1_cout), .Sum(n4bitadder_2_sum[0]), .Sum_2(n4bitadder_2_sum[1]),
    .Sum_3(n4bitadder_2_sum[2]), .Sum_4(n4bitadder_2_sum[3]), .Cout(n4bitadder_2_cout));
  _7segEncoder u_7segencoder_1 (
    .in_2(register_1_out_11[1]), .in_3(register_1_out_11[2]), .in_4(register_1_out_11[3]),
    .in_1(register_1_out_11[0]), .out_5(n7segencoder_1_out_5), .out_6(n7segencoder_1_out_6),
    .out_7(n7segencoder_1_out_7), .out_8(n7segencoder_1_out_8), .out_9(n7segencoder_1_out_9),
    .out_10(n7segencoder_1_out_10), .out_11(n7segencoder_1_out_11));
  _7segEncoder u_7segencoder_2 (
    .in_2(register_1_out_11[5]), .in_3(register_1_out_11[6]), .in_4(register_1_out_11[7]),
    .in_1(register_1_out_11[4]), .out_5(n7segencoder_2_out_5), .out_6(n7segencoder_2_out_6),
    .out_7(n7segencoder_2_out_7), .out_8(n7segencoder_2_out_8), .out_9(n7segencoder_2_out_9),
    .out_10(n7segencoder_2_out_10), .out_11(n7segencoder_2_out_11));
  CarryBit carrybit_1 (
    ._5(carrybit_1__6[1]), ._0(carrybit_1__3[3]), ._3(carrybit_1__3[0]), ._6(carrybit_1__6[0]),
    ._1(carrybit_1__3[2]), ._2(carrybit_1__3[1]), ._4(carrybit_1__6[2]), .in_1(Subtraction),
    .in_2(n4bitadder_2_cout));
  _7segEncoder u_7segencoder_3 (
    .in_2(register_2_out_11[1]), .in_3(register_2_out_11[2]), .in_4(register_2_out_11[3]),
    .in_1(register_2_out_11[0]), .out_5(n7segencoder_3_out_5), .out_6(n7segencoder_3_out_6),
    .out_7(n7segencoder_3_out_7), .out_8(n7segencoder_3_out_8), .out_9(n7segencoder_3_out_9),
    .out_10(n7segencoder_3_out_10), .out_11(n7segencoder_3_out_11));
  _7segEncoder u_7segencoder_4 (
    .in_2(register_2_out_11[5]), .in_3(register_2_out_11[6]), .in_4(register_2_out_11[7]),
    .in_1(register_2_out_11[4]), .out_5(n7segencoder_4_out_5), .out_6(n7segencoder_4_out_6),
    .out_7(n7segencoder_4_out_7), .out_8(n7segencoder_4_out_8), .out_9(n7segencoder_4_out_9),
    .out_10(n7segencoder_4_out_10), .out_11(n7segencoder_4_out_11));
  Register register_3 (
    .Clk(clock_1_out), .En(SumIn), .D(n4bitadder_1_sum[0]), .D_2(n4bitadder_1_sum[1]),
    .D_3(n4bitadder_1_sum[2]), .D_4(n4bitadder_1_sum[3]), .D_5(n4bitadder_2_sum[0]),
    .D_6(n4bitadder_2_sum[1]), .D_7(n4bitadder_2_sum[2]), .D_8(n4bitadder_2_sum[3]),
    .out_11(register_3_out_11[0]), .out_12(register_3_out_11[1]), .out_13(register_3_out_11[2]),
    .out_14(register_3_out_11[3]), .out_15(register_3_out_15[0]), .out_16(register_3_out_15[1]),
    .out_17(register_3_out_15[2]), .out_18(register_3_out_15[3]));
  _7_Segment_Display u_7_segment_display_1 (
    .g(n7segencoder_2_out_11), .f(n7segencoder_2_out_10), .a(n7segencoder_2_out_9), .b(n7segencoder_2_out_8),
    .e(n7segencoder_2_out_7), .d(n7segencoder_2_out_6), .c(n7segencoder_2_out_5));  // open: dp
  _7_Segment_Display u_7_segment_display_2 (
    .g(n7segencoder_1_out_11), .f(n7segencoder_1_out_10), .a(n7segencoder_1_out_9), .b(n7segencoder_1_out_8),
    .e(n7segencoder_1_out_7), .d(n7segencoder_1_out_6), .c(n7segencoder_1_out_5));  // open: dp
  _7_Segment_Display u_7_segment_display_3 (
    .g(n7segencoder_4_out_11), .f(n7segencoder_4_out_10), .a(n7segencoder_4_out_9), .b(n7segencoder_4_out_8),
    .e(n7segencoder_4_out_7), .d(n7segencoder_4_out_6), .c(n7segencoder_4_out_5));  // open: dp
  _7segEncoder u_7segencoder_5 (
    .in_2(register_3_out_11[1]), .in_3(register_3_out_11[2]), .in_4(register_3_out_11[3]),
    .in_1(register_3_out_11[0]), .out_5(n7segencoder_5_out_5[0]), .out_6(n7segencoder_5_out_5[1]),
    .out_7(n7segencoder_5_out_5[2]), .out_8(n7segencoder_5_out_8[0]), .out_9(n7segencoder_5_out_8[1]),
    .out_10(n7segencoder_5_out_8[2]), .out_11(n7segencoder_5_out_8[3]));
  _7segEncoder u_7segencoder_6 (
    .in_2(register_3_out_15[1]), .in_3(register_3_out_15[2]), .in_4(register_3_out_15[3]),
    .in_1(register_3_out_15[0]), .out_5(n7segencoder_6_out_5[0]), .out_6(n7segencoder_6_out_5[1]),
    .out_7(n7segencoder_6_out_5[2]), .out_8(n7segencoder_6_out_8[0]), .out_9(n7segencoder_6_out_8[1]),
    .out_10(n7segencoder_6_out_8[2]), .out_11(n7segencoder_6_out_8[3]));
  _7_Segment_Display u_7_segment_display_4 (
    .g(n7segencoder_3_out_11), .f(n7segencoder_3_out_10), .a(n7segencoder_3_out_9), .b(n7segencoder_3_out_8),
    .e(n7segencoder_3_out_7), .d(n7segencoder_3_out_6), .c(n7segencoder_3_out_5));  // open: dp
  _7_Segment_Display u_7_segment_display_5 (
    .g(carrybit_1__3[3]), .f(carrybit_1__3[2]), .a(carrybit_1__3[1]), .b(carrybit_1__3[0]),
    .e(carrybit_1__6[2]), .d(carrybit_1__6[1]), .c(carrybit_1__6[0]));  // open: dp
  _7_Segment_Display u_7_segment_display_6 (
    .g(n7segencoder_5_out_8[3]), .f(n7segencoder_5_out_8[2]), .a(n7segencoder_5_out_8[1]),
    .b(n7segencoder_5_out_8[0]), .e(n7segencoder_5_out_5[2]), .d(n7segencoder_5_out_5[1]),
    .c(n7segencoder_5_out_5[0]));  // open: dp
  _7_Segment_Display u_7_segment_display_7 (
    .g(n7segencoder_6_out_8[3]), .f(n7segencoder_6_out_8[2]), .a(n7segencoder_6_out_8[1]),
    .b(n7segencoder_6_out_8[0]), .e(n7segencoder_6_out_5[2]), .d(n7segencoder_6_out_5[1]),
    .c(n7segencoder_6_out_5[0]));  // open: dp

  // Notes on the sheet:
  //   Aout
  //   Ain
  //   Bout
  //   Bin
  //   SumOut
  //   SumIn
  //   Subtraction
  //   A2S
  //   B2S
  //   PCout
  //   MARin
  //   MARout
  //   IPin
  //   IPout
  //   RAM load
  //   RAM read
  //   Value to Bus
endmodule

module _7segEncoder (
  input  in_1,
  input  in_2,
  input  in_3,
  input  in_4,
  output out_5,
  output out_6,
  output out_7,
  output out_8,
  output out_9,
  output out_10,
  output out_11
);

  wire and_1_out, and_2_out, and_3_out, and_4_out, and_5_out, and_6_out, and_7_out, and_8_out, and_9_out,
       and_10_out, and_11_out, and_12_out, and_13_out, and_14_out, and_15_out, and_16_out, and_17_out,
       and_18_out, and_19_out, and_20_out, and_21_out, and_22_out, and_23_out, and_24_out, and_25_out,
       and_26_out, and_27_out, and_28_out, and_29_out, and_30_out, and_31_out, and_32_out, not_1_out,
       not_2_out, not_3_out, not_4_out, or_1_out, or_2_out, or_4_out;

  not not_1 (not_1_out, in_3);
  not not_2 (not_2_out, in_4);
  not not_3 (not_3_out, in_1);
  not not_4 (not_4_out, in_2);
  or or_1 (or_1_out, in_3, not_4_out, in_1);
  or or_2 (or_2_out, in_3, in_2);
  and and_1 (and_1_out, not_2_out, or_1_out);
  and and_2 (and_2_out, not_4_out, in_1);
  and and_3 (and_3_out, in_4, not_1_out);
  and and_4 (and_4_out, in_3, not_4_out, in_1);
  and and_5 (and_5_out, in_3, in_2, not_3_out);
  and and_6 (and_6_out, not_2_out, not_1_out, not_3_out);
  and and_7 (and_7_out, not_1_out, in_2, in_1);
  and and_8 (and_8_out, in_4, not_4_out, not_3_out);
  and and_9 (and_9_out, or_2_out, in_4);
  and and_10 (and_10_out, not_1_out, not_4_out);
  and and_11 (and_11_out, not_2_out, in_2);
  and and_12 (and_12_out, in_3, in_2);
  and and_13 (and_13_out, in_4, not_3_out);
  and and_14 (and_14_out, not_2_out, in_3, in_1);
  and and_15 (and_15_out, in_4, not_1_out, not_4_out);
  and and_16 (and_16_out, not_1_out, not_4_out, not_3_out);
  or or_3 (out_5, and_1_out, and_2_out, and_3_out);
  or or_4 (or_4_out, and_10_out, in_2);
  and and_17 (and_17_out, or_4_out, not_3_out);
  and and_18 (and_18_out, not_2_out, not_1_out);
  and and_19 (and_19_out, not_2_out, not_4_out, not_3_out);
  and and_20 (and_20_out, not_2_out, in_2, in_1);
  and and_21 (and_21_out, in_4, not_4_out, in_1);
  and and_22 (and_22_out, in_4, not_1_out, not_3_out);
  and and_23 (and_23_out, not_4_out, not_3_out);
  and and_24 (and_24_out, in_4, in_2);
  and and_25 (and_25_out, in_4, not_1_out);
  and and_26 (and_26_out, not_2_out, in_3, not_4_out);
  and and_27 (and_27_out, in_3, in_2, not_3_out);
  and and_28 (and_28_out, in_2, not_3_out);
  and and_29 (and_29_out, in_1, in_4);
  and and_30 (and_30_out, in_4, not_1_out);
  and and_31 (and_31_out, not_2_out, in_3, not_4_out);
  and and_32 (and_32_out, not_2_out, not_1_out, in_2);
  or or_5 (out_6, and_4_out, and_5_out, and_8_out, and_6_out, and_7_out);
  or or_6 (out_8, and_18_out, and_19_out, and_20_out, and_21_out, and_22_out);
  or or_7 (out_9, and_11_out, and_12_out, and_13_out, and_14_out, and_15_out, and_16_out, and_16_out);
  or or_8 (out_7, and_9_out, and_17_out);
  or or_9 (out_10, and_23_out, and_24_out, and_25_out, and_26_out, and_27_out);
  or or_10 (out_11, and_28_out, and_29_out, and_30_out, and_31_out, and_32_out);

  // Notes on the sheet:
  //   W
  //   B0
  //   B1
  //   X
  //   X
  //   W
  //   B2
  //   B3
  //   Z
  //   Y
  //   Y
  //   Z
  //   Result first digit display Logic (S6 top-S0 bottom)
endmodule

module _8bitadder (
  input  in_1,
  input  in_2,
  input  in_3,
  input  in_4,
  input  in_5,
  input  in_6,
  input  in_7,
  input  in_8,
  input  in_9,
  input  in_10,
  input  in_11,
  input  in_12,
  input  in_13,
  input  in_14,
  input  in_15,
  input  in_16,
  output out_17,
  output Sum,
  output Sum_2,
  output Sum_3,
  output Sum_4,
  output Sum_5,
  output Sum_6,
  output Sum_7,
  output Cout
);

  wire and_1_out, and_2_out, and_3_out, and_4_out, and_5_out, and_6_out, and_7_out, and_8_out, and_9_out,
       and_10_out, and_11_out, and_12_out, and_13_out, and_14_out, and_15_out, and_16_out, or_1_out,
       or_2_out, or_3_out, or_4_out, or_5_out, or_6_out, or_7_out, xor_1_out, xor_2_out, xor_5_out,
       xor_6_out, xor_9_out, xor_10_out, xor_13_out, xor_14_out;

  xor xor_1 (xor_1_out, in_1, in_5);
  xor xor_2 (xor_2_out, in_9, in_13);
  and and_1 (and_1_out, 1'b0, xor_1_out);
  and and_2 (and_2_out, in_1, in_5);
  and and_3 (and_3_out, or_7_out, xor_2_out);
  and and_4 (and_4_out, in_9, in_13);
  xor xor_3 (out_17, xor_1_out, 1'b0);
  or or_1 (or_1_out, and_1_out, and_2_out);
  xor xor_4 (Sum_4, xor_2_out, or_7_out);
  or or_2 (or_2_out, and_3_out, and_4_out);
  xor xor_5 (xor_5_out, in_2, in_6);
  xor xor_6 (xor_6_out, in_10, in_14);
  and and_5 (and_5_out, or_1_out, xor_5_out);
  and and_6 (and_6_out, in_2, in_6);
  and and_7 (and_7_out, or_2_out, xor_6_out);
  and and_8 (and_8_out, in_10, in_14);
  xor xor_7 (Sum, xor_5_out, or_1_out);
  or or_3 (or_3_out, and_5_out, and_6_out);
  xor xor_8 (Sum_5, xor_6_out, or_2_out);
  or or_4 (or_4_out, and_7_out, and_8_out);
  xor xor_9 (xor_9_out, in_3, in_7);
  xor xor_10 (xor_10_out, in_11, in_15);
  and and_9 (and_9_out, or_3_out, xor_9_out);
  and and_10 (and_10_out, in_3, in_7);
  and and_11 (and_11_out, or_4_out, xor_10_out);
  and and_12 (and_12_out, in_11, in_15);
  xor xor_11 (Sum_2, xor_9_out, or_3_out);
  or or_5 (or_5_out, and_9_out, and_10_out);
  xor xor_12 (Sum_6, xor_10_out, or_4_out);
  or or_6 (or_6_out, and_11_out, and_12_out);
  xor xor_13 (xor_13_out, in_4, in_8);
  xor xor_14 (xor_14_out, in_12, in_16);
  and and_13 (and_13_out, or_5_out, xor_13_out);
  and and_14 (and_14_out, in_4, in_8);
  and and_15 (and_15_out, or_6_out, xor_14_out);
  and and_16 (and_16_out, in_12, in_16);
  xor xor_15 (Sum_3, xor_13_out, or_5_out);
  or or_7 (or_7_out, and_13_out, and_14_out);
  xor xor_16 (Sum_7, xor_14_out, or_6_out);
  or or_8 (Cout, and_15_out, and_16_out);

  // Notes on the sheet:
  //   Sum
  //   Cout
  //   Cout
  //   Cout
  //   Cout
  //   Cout
  //   Cout
  //   Cout
endmodule

module RAM (
);

  wire undriven, undriven_2;

  RAM_part ram_1 (.sel(undriven), .clk(undriven_2));  // open: addr, data, ld, clr
endmodule

module Register (
  input  Clk,
  input  En,
  input  D,
  input  D_2,
  input  D_3,
  input  D_4,
  input  D_5,
  input  D_6,
  input  D_7,
  input  D_8,
  output out_11,
  output out_12,
  output out_13,
  output out_14,
  output out_15,
  output out_16,
  output out_17,
  output out_18
);

  wire and_1_out, and_2_out, and_3_out, and_4_out, and_5_out, and_6_out, and_7_out, and_8_out, and_9_out,
       and_10_out, and_11_out, and_12_out, and_13_out, and_14_out, and_15_out, and_16_out, d_ff_1_q,
       d_ff_2_q, d_ff_3_q, d_ff_4_q, d_ff_5_q, d_ff_6_q, d_ff_7_q, d_ff_8_q, not_1_out, not_2_out, not_3_out,
       not_4_out, not_5_out, not_6_out, not_7_out, not_8_out, or_1_out, or_2_out, or_3_out, or_4_out,
       or_5_out, or_6_out, or_7_out, or_8_out;

  not not_1 (not_1_out, En);
  not not_2 (not_2_out, En);
  not not_3 (not_3_out, En);
  not not_4 (not_4_out, En);
  not not_5 (not_5_out, En);
  not not_6 (not_6_out, En);
  not not_7 (not_7_out, En);
  not not_8 (not_8_out, En);
  and and_1 (and_1_out, d_ff_1_q, not_1_out);
  and and_2 (and_2_out, En, D);
  and and_3 (and_3_out, d_ff_2_q, not_2_out);
  and and_4 (and_4_out, En, D_2);
  and and_5 (and_5_out, d_ff_3_q, not_3_out);
  and and_6 (and_6_out, En, D_3);
  and and_7 (and_7_out, d_ff_4_q, not_4_out);
  and and_8 (and_8_out, En, D_4);
  and and_9 (and_9_out, d_ff_5_q, not_5_out);
  and and_10 (and_10_out, En, D_5);
  and and_11 (and_11_out, d_ff_6_q, not_6_out);
  and and_12 (and_12_out, En, D_6);
  and and_13 (and_13_out, d_ff_7_q, not_7_out);
  and and_14 (and_14_out, En, D_7);
  and and_15 (and_15_out, d_ff_8_q, not_8_out);
  and and_16 (and_16_out, En, D_8);
  or or_1 (or_1_out, and_1_out, and_2_out);
  or or_2 (or_2_out, and_3_out, and_4_out);
  or or_3 (or_3_out, and_5_out, and_6_out);
  or or_4 (or_4_out, and_7_out, and_8_out);
  or or_5 (or_5_out, and_9_out, and_10_out);
  or or_6 (or_6_out, and_11_out, and_12_out);
  or or_7 (or_7_out, and_13_out, and_14_out);
  or or_8 (or_8_out, and_15_out, and_16_out);
  D_Flip_Flop d_ff_1 (.clk(Clk), .D(or_1_out), .Q(d_ff_1_q));  // open: Qn, preset, en, reset
  D_Flip_Flop d_ff_2 (.clk(Clk), .D(or_2_out), .Q(d_ff_2_q));  // open: Qn, preset, en, reset
  D_Flip_Flop d_ff_3 (.clk(Clk), .D(or_3_out), .Q(d_ff_3_q));  // open: Qn, preset, en, reset
  D_Flip_Flop d_ff_4 (.clk(Clk), .D(or_4_out), .Q(d_ff_4_q));  // open: Qn, preset, en, reset
  D_Flip_Flop d_ff_5 (.clk(Clk), .D(or_5_out), .Q(d_ff_5_q));  // open: Qn, preset, en, reset
  D_Flip_Flop d_ff_6 (.clk(Clk), .D(or_6_out), .Q(d_ff_6_q));  // open: Qn, preset, en, reset
  D_Flip_Flop d_ff_7 (.clk(Clk), .D(or_7_out), .Q(d_ff_7_q));  // open: Qn, preset, en, reset
  D_Flip_Flop d_ff_8 (.clk(Clk), .D(or_8_out), .Q(d_ff_8_q));  // open: Qn, preset, en, reset
  assign out_11 = 1'b1 ? d_ff_1_q : 1'bz;  // Controlled_Buffer controlled_buffer_1
  assign out_12 = 1'b1 ? d_ff_2_q : 1'bz;  // Controlled_Buffer controlled_buffer_2
  assign out_13 = 1'b1 ? d_ff_3_q : 1'bz;  // Controlled_Buffer controlled_buffer_3
  assign out_14 = 1'b1 ? d_ff_4_q : 1'bz;  // Controlled_Buffer controlled_buffer_4
  assign out_15 = 1'b1 ? d_ff_5_q : 1'bz;  // Controlled_Buffer controlled_buffer_5
  assign out_16 = 1'b1 ? d_ff_6_q : 1'bz;  // Controlled_Buffer controlled_buffer_6
  assign out_17 = 1'b1 ? d_ff_7_q : 1'bz;  // Controlled_Buffer controlled_buffer_7
  assign out_18 = 1'b1 ? d_ff_8_q : 1'bz;  // Controlled_Buffer controlled_buffer_8

  // Notes on the sheet:
  //   ~Q
  //   ~Q
  //   ~Q
  //   ~Q
  //   ~Q
  //   ~Q
  //   ~Q
  //   ~Q
  //   Q
  //   Q
  //   Q
  //   Q
  //   Q
  //   Q
  //   Q
  //   Q
endmodule

module _4bitadder (
  input  in_1,
  input  in_2,
  input  in_3,
  input  in_4,
  input  in_5,
  input  in_6,
  input  in_7,
  input  in_8,
  input  in_9,
  output Sum,
  output Sum_2,
  output Sum_3,
  output Sum_4,
  output Cout
);

  wire and_1_out, and_2_out, and_3_out, and_4_out, and_5_out, and_6_out, and_7_out, and_8_out, or_1_out,
       or_2_out, or_3_out, xor_1_out, xor_3_out, xor_5_out, xor_7_out;

  xor xor_1 (xor_1_out, in_1, in_5);
  and and_1 (and_1_out, in_9, xor_1_out);
  and and_2 (and_2_out, in_1, in_5);
  xor xor_2 (Sum, xor_1_out, in_9);
  or or_1 (or_1_out, and_1_out, and_2_out);
  xor xor_3 (xor_3_out, in_2, in_6);
  and and_3 (and_3_out, or_1_out, xor_3_out);
  and and_4 (and_4_out, in_2, in_6);
  xor xor_4 (Sum_2, xor_3_out, or_1_out);
  or or_2 (or_2_out, and_3_out, and_4_out);
  xor xor_5 (xor_5_out, in_3, in_7);
  and and_5 (and_5_out, or_2_out, xor_5_out);
  and and_6 (and_6_out, in_3, in_7);
  xor xor_6 (Sum_3, xor_5_out, or_2_out);
  or or_3 (or_3_out, and_5_out, and_6_out);
  xor xor_7 (xor_7_out, in_4, in_8);
  and and_7 (and_7_out, or_3_out, xor_7_out);
  and and_8 (and_8_out, in_4, in_8);
  xor xor_8 (Sum_4, xor_7_out, or_3_out);
  or or_4 (Cout, and_7_out, and_8_out);

  // Notes on the sheet:
  //   Cout
  //   Cout
  //   Cout
endmodule

module CarryBit (
  input  in_1,
  input  in_2,
  output _5,
  output _0,
  output _3,
  output _6,
  output _1,
  output _2,
  output _4
);

  wire not_1_out, not_2_out;

  not not_1 (not_1_out, in_1);
  not not_2 (not_2_out, in_2);
  nand nand_1 (_1, in_2, not_1_out);
  xnor xnor_1 (_5, in_1, in_2);
  and and_1 (_0, in_1, not_2_out);
  not not_3 (_3, _0);

  assign _2 = _1;
  assign _4 = _1;
  assign _6 = _3;
endmodule

module _4bitRegister (
  input  Clk,
  input  En,
  input  D,
  input  in_4,
  input  D_2,
  input  D_3,
  input  D_4,
  output out_8,
  output out_9,
  output out_10,
  output out_11
);

  wire and_1_out, and_2_out, and_3_out, and_4_out, and_5_out, and_6_out, and_7_out, and_8_out, d_ff_1_q,
       d_ff_2_q, d_ff_3_q, d_ff_4_q, not_1_out, not_2_out, not_3_out, not_4_out, or_1_out, or_2_out,
       or_3_out, or_4_out;

  not not_1 (not_1_out, En);
  not not_2 (not_2_out, En);
  not not_3 (not_3_out, En);
  not not_4 (not_4_out, En);
  and and_1 (and_1_out, d_ff_1_q, not_1_out);
  and and_2 (and_2_out, En, D);
  and and_3 (and_3_out, d_ff_2_q, not_2_out);
  and and_4 (and_4_out, En, D_2);
  and and_5 (and_5_out, d_ff_3_q, not_3_out);
  and and_6 (and_6_out, En, D_3);
  and and_7 (and_7_out, d_ff_4_q, not_4_out);
  and and_8 (and_8_out, En, D_4);
  or or_1 (or_1_out, and_1_out, and_2_out);
  or or_2 (or_2_out, and_3_out, and_4_out);
  or or_3 (or_3_out, and_5_out, and_6_out);
  or or_4 (or_4_out, and_7_out, and_8_out);
  D_Flip_Flop d_ff_1 (.clk(Clk), .D(or_1_out), .Q(d_ff_1_q), .reset(in_4));  // open: Qn, preset, en
  D_Flip_Flop d_ff_2 (.clk(Clk), .D(or_2_out), .Q(d_ff_2_q), .reset(in_4));  // open: Qn, preset, en
  D_Flip_Flop d_ff_3 (.clk(Clk), .D(or_3_out), .Q(d_ff_3_q), .reset(in_4));  // open: Qn, preset, en
  D_Flip_Flop d_ff_4 (.clk(Clk), .D(or_4_out), .Q(d_ff_4_q), .reset(in_4));  // open: Qn, preset, en
  assign out_8 = 1'b1 ? d_ff_1_q : 1'bz;  // Controlled_Buffer controlled_buffer_1
  assign out_9 = 1'b1 ? d_ff_2_q : 1'bz;  // Controlled_Buffer controlled_buffer_2
  assign out_10 = 1'b1 ? d_ff_3_q : 1'bz;  // Controlled_Buffer controlled_buffer_3
  assign out_11 = 1'b1 ? d_ff_4_q : 1'bz;  // Controlled_Buffer controlled_buffer_4

  // Notes on the sheet:
  //   ~Q
  //   ~Q
  //   ~Q
  //   ~Q
  //   Q
  //   Q
  //   Q
  //   Q
endmodule
